# Fritzing sketch Sensor de linea (saved by Fritzing 0.9.2b)
circuit board: 14.7359cm x 20.021cm
breadboards: 1

parts:
  R2 = TRIMPOT [package=trim_pot_pth]
  pT1 = LTR-301 [package=ltr-301]
  R3 = Resistor [tolerance=±5% resistance=220 package=THT]
  pT2 = LTR-301 [package=ltr-301]
  R4 = Resistor [tolerance=±5% resistance=220 package=THT]
  pT3 = LTR-301 [package=ltr-301]
  R5 = Resistor [tolerance=±5% resistance=220 package=THT]
  pT4 = LTR-301 [package=ltr-301]
  R6 = Resistor [tolerance=±5% resistance=220 package=THT]
  pT5 = LTR-301 [package=ltr-301]
  R7 = Resistor [tolerance=±5% resistance=220 package=THT]
  pT6 = LTR-301 [package=ltr-301]
  R8 = Resistor [tolerance=±5% resistance=220 package=THT]
  pT7 = LTR-301 [package=ltr-301]
  R9 = Resistor [tolerance=±5% resistance=220 package=THT]
  pT8 = LTR-301 [package=ltr-301]
  R10 = Resistor [tolerance=±5% resistance=220 package=THT]
  Atmega328 = MICROCONTROLLER [package=dil28-3]
  S1 = SWITCH-MOMENTARY-2 [package=tactile-pth]
  R11 = Resistor [tolerance=±5% resistance=10k package=THT]
  XTAL1 = Crystal [frequency="16 Mhz" package=THT]
  C1 = Ceramic Capacitor [capacitance=22pF package="0603 [SMD, multilayer]"]
  C2 = Ceramic Capacitor [capacitance=22pF package="0603 [SMD, multilayer]"]
  HC-SR04_F = female pin header, 4 pins [form="♀ (female)"]
  IC2 = Voltage Regulator [package=to-220-alt]
  C3 = Electrolytic Capacitor [capacitance=1µF voltage=16V package="100 mil [THT, electrolytic]"]
  C4 = Electrolytic Capacitor [capacitance=10µF voltage=16V package="100 mil [THT, electrolytic]"]
  D1 = Diode [package=diode-1n4001]
  HC-SR04_L = female pin header, 4 pins [form="♀ (female)"]
  mDriver = ULN2003A [package="DIP16 [THT]"]
  Motor1 = female pin header, 2 pins [form="♀ (female)"]
  Motor2 = female pin header, 2 pins [form="♀ (female)"]
  Infra1 = LED - 5mm [color="Red (633nm)" package="5 mm [THT]"]
  RInf1 = Resistor [tolerance=±5% resistance=33 package=THT]
  RInf2 = Resistor [tolerance=±5% resistance=33 package=THT]
  Infra2 = LED - 5mm [color="Red (633nm)" package="5 mm [THT]"]
  RInf3 = Resistor [tolerance=±5% resistance=33 package=THT]
  Infra3 = LED - 5mm [color="Red (633nm)" package="5 mm [THT]"]
  RInf4 = Resistor [tolerance=±5% resistance=33 package=THT]
  Infra4 = LED - 5mm [color="Red (633nm)" package="5 mm [THT]"]
  RInf8 = Resistor [tolerance=±5% resistance=33 package=THT]
  RInf7 = Resistor [tolerance=±5% resistance=33 package=THT]
  RInf6 = Resistor [tolerance=±5% resistance=33 package=THT]
  RInf5 = Resistor [tolerance=±5% resistance=33 package=THT]
  Infra5 = LED - 5mm [color="Red (633nm)" package="5 mm [THT]"]
  Infra6 = LED - 5mm [color="Red (633nm)" package="5 mm [THT]"]
  Infra8 = LED - 5mm [color="Red (633nm)" package="5 mm [THT]"]
  Infra7 = LED - 5mm [color="Red (633nm)" package="5 mm [THT]"]
  C5 = Electrolytic Capacitor [capacitance=10µF voltage=10V package="100 mil [THT, electrolytic]"]
  LM324_1 = IC, DIP package, 14 pins [chip_label=LM324]
  C_324_1 = Electrolytic Capacitor [capacitance=1µF package="100 mil [THT, electrolytic]"]
  LM324_2 = IC, DIP package, 14 pins [chip_label=LM324]
  C_324_2 = Electrolytic Capacitor [capacitance=1µF package="100 mil [THT, electrolytic]"]

nets:
  5V: R2.CCW, R3.Pin_0, R4.Pin_0, R5.Pin_0, R6.Pin_0, R7.Pin_0, R8.Pin_0, R9.Pin_0, R10.Pin_0, Atmega328.VCC, Atmega328.AVCC, R11.Pin_0, HC-SR04_F.pin1, IC2.OUT, C3.+, HC-SR04_L.pin1, RInf1.Pin_0, RInf2.Pin_0, RInf3.Pin_0, RInf4.Pin_0, RInf8.Pin_0, RInf7.Pin_0, RInf6.Pin_0, RInf5.Pin_0, C5.+, LM324_1.pin4, C_324_1.+, LM324_2.pin4, C_324_2.+
  vPot: R2.WIPER, LM324_1.pin2, LM324_1.pin6, LM324_1.pin9, LM324_1.pin13, LM324_2.pin2, LM324_2.pin6, LM324_2.pin9, LM324_2.pin13
  GND: R2.CW, pT1.E, pT2.E, pT3.E, pT4.E, pT5.E, pT6.E, pT7.E, pT8.E, Atmega328.GND, Atmega328.AGND, S1.1, C1.1, C2.1, HC-SR04_F.pin4, IC2.GND, C3.-, C4.-, D1.A, HC-SR04_L.pin4, mDriver.0V, Infra1.cathode, Infra2.cathode, Infra3.cathode, Infra4.cathode, Infra5.cathode, Infra6.cathode, Infra8.cathode, Infra7.cathode, C5.-, LM324_1.pin11, C_324_1.-, LM324_2.pin11, C_324_2.-
  vpT1: pT1.C, R3.Pin_1, LM324_1.pin3
  vpT2: pT2.C, R4.Pin_1, LM324_1.pin5
  vpT3: pT3.C, R5.Pin_1, LM324_1.pin10
  vpT4: pT4.C, R6.Pin_1, LM324_1.pin12
  vpT5: pT5.C, R7.Pin_1, LM324_2.pin3
  vpT6: pT6.C, R8.Pin_1, LM324_2.pin5
  vpT7: pT7.C, R9.Pin_1, LM324_2.pin10
  vpT8: pT8.C, R10.Pin_1, LM324_2.pin12
  N1: Atmega328.PC6(_RESET), S1.2, R11.Pin_1
  p1: Atmega328.PD2(INT0), LM324_1.pin1
  TriggerF: Atmega328.PD3(INT1), HC-SR04_F.pin2
  p2: Atmega328.PD4(XCK_T0), LM324_1.pin7
  N2: Atmega328.PB6(XTAL1_TOSC1), XTAL1.pin_1, C1.0
  N3: Atmega328.PB7(XTAL2_TOSC2), XTAL1.pin_0, C2.0
  MPin1: Atmega328.PD5(T1), mDriver.In_1
  MPin2: Atmega328.PD6(AIN0), mDriver.In_2
  p3: Atmega328.PD7(AIN1), LM324_1.pin8
  p4: Atmega328.PB0(ICP), LM324_1.pin14
  EchoF: Atmega328.PB1(OC1A), HC-SR04_F.pin3
  TriggerL: Atmega328.PB2(SS_OC1B), HC-SR04_L.pin2
  EchoL: Atmega328.PB3(MOSI_OC2), HC-SR04_L.pin3
  p5: Atmega328.PB4(MISO), LM324_2.pin1
  p6: Atmega328.PB5(SCK), LM324_2.pin7
  p7: Atmega328.PC0(ADC0), LM324_2.pin8
  p8: Atmega328.PC1(ADC1), LM324_2.pin14
  12V: IC2.IN, C4.+, D1.C, mDriver.COM_-_Common, Motor1.pin2, Motor2.pin2
  N4: mDriver.Out_2, Motor2.pin1
  N5: mDriver.Out_1, Motor1.pin1
  N6: Infra1.anode, RInf1.Pin_1
  N7: RInf2.Pin_1, Infra2.anode
  N8: RInf3.Pin_1, Infra3.anode
  N9: RInf4.Pin_1, Infra4.anode
  N10: RInf8.Pin_1, Infra8.anode
  N11: RInf7.Pin_1, Infra7.anode
  N12: RInf6.Pin_1, Infra6.anode
  N13: RInf5.Pin_1, Infra5.anode
